// Digital circuit fpga.dig as structural Verilog
module fpga (
  input  push,
  input  [2:0] i,
  input  pop,
  input  we_nostos,
  input  clk,
  input  mux_itos,
  input  mux_ytos,
  output [15:0] ros,
  output [15:0] tos,
  output [11:0] sp,
  output [15:0] nos,
  output [15:0] o,
  output [7:0] tos_2
);

  wire [2:0] counter_1_out;
  wire [2:1] undriven_2;
  wire [7:0] multiplexer_1_out;
  wire [12:3] undriven;

  Counter #(.Bits(3)) counter_1 (.en(1'b1), .C(clk), .clr(1'b0), .out(counter_1_out));  // open: ovf
  Multiplexer #(.Bits(8), .Selector_Bits(3)) multiplexer_1 (
    .sel(counter_1_out), .in_0({8{1'b0}}), .in_1({8{1'b0}}), .in_2({8{1'b0}}), .in_3({8{1'b0}}),
    .in_4({8{1'b0}}), .in_5({8{1'b0}}), .in_6({8{1'b0}}), .in_7({8{1'b0}}), .out(multiplexer_1_out));
  stack stack_1 (
    .clk(clk), .push(multiplexer_1_out[0]), .pop(multiplexer_1_out[1]),
    .i({undriven, multiplexer_1_out[7:5], undriven_2, 1'b0}), .y(o), .we_nostos(multiplexer_1_out[2]),
    .we_itos(multiplexer_1_out[3]), .we_ytos(multiplexer_1_out[4]), .tos(tos), .ros(ros), .nos(nos), .sp(sp));
  Add #(.Bits(16)) add_1 (.a(nos), .b(tos), .c_i(1'b0), .s(o));  // open: c_o
  // Pins of 3 and 13 bits meet at {undriven, multiplexer_1_out[7:5]}
  // Pins of 1 and 3 bits meet at {undriven_2, 1'b0}

  assign tos_2 = {i, mux_ytos, mux_itos, we_nostos, pop, push};

  // Other names for the same wires on the sheet: c = clk
endmodule
